# Fritzing sketch auto bt (saved by Fritzing 0.8.5b)
circuit board: 8.46667cm x 5.64444cm

parts:
  Part2 = Arduino Motor Shield (Rev3)
  J1 = Basic Servo
  Parte1 = Arduino Uno (Rev3)
  Parte2 = Bluetooth HC-05 Macho
  M1 = DC Motor

nets:
  GND: Part2.GND, J1.gnd, M1.pin_1
  5V: Part2.5V, J1.vcc
  N1: Part2.D9/BreakeA, J1.pulse
  N2: Part2.A-, M1.pin_2
  N3: Parte1.D0/RX, Parte2.TXD
  N4: Parte1.D1/TX, Parte2.RXD
  5V_2: Parte1.5V, Parte2.VCC
  GND_2: Parte1.GND, Parte2.GND
